// Logisim project NAND-y-XOR.circ as structural Verilog: 1 circuit, main circuit main
module main (
  input  a,
  input  b,
  input  a_2,
  input  b_2,
  input  a_3,
  input  b_3
);

  wire and_1_out, nand_1_out, not_1_out, not_2_out, not_3_out, not_4_out, or_1_out, or_2_out, or_3_out,
       xor_1_out;

  not not_1 (not_1_out, a_2);
  not not_2 (not_2_out, b_2);
  not not_3 (not_3_out, a);
  not not_4 (not_4_out, b);
  or or_1 (or_1_out, not_3_out, not_4_out);
  or or_2 (or_2_out, not_1_out, b_2);
  or or_3 (or_3_out, not_2_out, a_2);
  xor xor_1 (xor_1_out, a_3, b_3);
  and and_1 (and_1_out, a_3, b_3);
  LED led_1 (.in(or_1_out));
  nand nand_1 (nand_1_out, or_2_out, or_3_out);
  LED led_2 (.in(xor_1_out));
  LED led_3 (.in(and_1_out));
  LED led_4 (.in(nand_1_out));

  // Notes on the sheet:
  //   NAND
  //   XOR
endmodule
