// Logisim project Practica 6.circ as structural Verilog: 5 circuits, main circuit main
module main (
);
endmodule

module Ejercicio_1 (
  input  P,
  input  Q,
  input  P_2,
  input  Q_2
);

  wire and_1_out, and_2_out, not_1_out, not_2_out, not_3_out, or_1_out, or_2_out;

  not not_1 (not_1_out, P);
  LED led_1 (.in(or_1_out));
  or or_1 (or_1_out, Q, not_1_out);
  not not_2 (not_2_out, Q_2);
  not not_3 (not_3_out, P_2);
  and and_1 (and_1_out, Q_2, P_2);
  and and_2 (and_2_out, not_2_out, not_3_out);
  LED led_2 (.in(or_2_out));
  or or_2 (or_2_out, and_1_out, and_2_out);

  // Notes on the sheet:
  //   → 
  //   P → Q ≡ ¬ P ∨ Q
  //   ↔
  //   P ↔ Q ≡ (P ∧ Q) ∨ (¬ P ∧ ¬ Q)
endmodule

module Ejercicio_2 (
  input  p,
  input  q,
  input  p_2,
  input  q_2,
  input  r
);

  wire and_1_out, and_2_out, or_1_out;

  or or_1 (or_1_out, q_2, p_2);
  and and_1 (and_1_out, q, p);
  and and_2 (and_2_out, r, or_1_out);
  LED led_1 (.in(and_1_out));
  LED led_2 (.in(and_2_out));

  // Notes on the sheet:
  //   a)
  //   b)
  //   Si el metro llega tarde o hay mucha gente y no me puedo subir, llegaré tarde a la facultad.
  //   (p ∨ q) ∧ r
  //   p: Tengo suficiente dinero.  q: No tengo nada más que hacer.    r: Iré al concierto.
  //   (p ∧ q) 
  //   p: El metro llega tarde.    q: Hay mucha gente.    r: No me puedo subir al metro.   s: Llegaré tarde a la facultad.
  //   Si tengo suficiente dinero y no tengo nada más que hacer, entonces iré al concierto, pero si no tengo suficiente dinero, no iré.
  //   Salida del circuito = s
  //   Salida del circuito = r
  //   r
  //   s
endmodule

module Ejercicio_3 (
  input  a,
  input  a_2,
  input  a_3,
  input  a_4,
  input  b,
  input  b_2,
  input  b_3,
  input  b_4,
  input  b_5,
  input  b_6,
  input  c,
  input  c_2,
  input  a_5,
  input  a_6,
  input  b_7,
  input  b_8,
  input  a_7,
  input  a_8,
  input  a_9,
  input  a_10,
  input  b_9,
  input  b_10,
  input  c_3,
  input  c_4,
  input  c_5,
  input  c_6,
  input  a_11,
  input  a_12,
  input  a_13,
  input  a_14,
  input  b_11,
  input  b_12,
  input  b_13,
  input  b_14,
  input  c_7,
  input  c_8,
  input  a_15,
  input  a_16,
  input  b_15,
  input  b_16,
  input  a_17,
  input  a_18,
  input  _0,
  input  _1,
  input  a_19,
  input  a_20,
  input  a_21,
  input  a_22,
  input  b_17,
  input  b_18,
  input  _1_2,
  input  _0_2,
  input  a_23,
  input  a_24,
  input  a_25,
  input  a_26
);

  wire and_1_out, and_2_out, and_3_out, and_4_out, and_5_out, and_6_out, and_7_out, and_8_out, and_9_out,
       and_10_out, and_11_out, and_12_out, and_13_out, and_14_out, and_15_out, and_16_out, and_17_out,
       and_18_out, and_19_out, not_1_out, not_2_out, not_3_out, not_4_out, not_5_out, not_6_out, not_7_out,
       not_8_out, or_1_out, or_2_out, or_3_out, or_4_out, or_5_out, or_6_out, or_7_out, or_8_out, or_9_out,
       or_10_out, or_11_out, or_12_out, or_13_out, or_14_out, or_15_out, or_16_out, or_17_out, or_18_out,
       or_19_out;

  or or_1 (or_1_out, a, b);
  or or_2 (or_2_out, b_5, a_5);
  or or_3 (or_3_out, b_9, c_5);
  or or_4 (or_4_out, a_11, b_11);
  or or_5 (or_5_out, a_17, _0);
  or or_6 (or_6_out, a_21, _1_2);
  or or_7 (or_7_out, a_23, not_1_out);
  not not_1 (not_1_out, a_23);
  LED led_1 (.in(or_1_out));
  LED led_2 (.in(or_2_out));
  or or_8 (or_8_out, a_7, or_3_out);
  or or_9 (or_9_out, or_4_out, c_7);
  LED led_3 (.in(or_5_out));
  LED led_4 (.in(or_6_out));
  LED led_5 (.in(or_7_out));
  LED led_6 (.in(or_8_out));
  LED led_7 (.in(or_9_out));
  and and_1 (and_1_out, a_2, b_2);
  and and_2 (and_2_out, b_6, a_6);
  and and_3 (and_3_out, a_18, _1);
  and and_4 (and_4_out, a_22, _0_2);
  and and_5 (and_5_out, a_24, not_2_out);
  not not_2 (not_2_out, a_24);
  LED led_8 (.in(and_1_out));
  LED led_9 (.in(and_2_out));
  and and_6 (and_6_out, b_10, c_6);
  and and_7 (and_7_out, a_12, b_12);
  LED led_10 (.in(and_3_out));
  LED led_11 (.in(and_4_out));
  LED led_12 (.in(and_5_out));
  and and_8 (and_8_out, a_8, and_6_out);
  LED led_13 (.in(and_8_out));
  and and_9 (and_9_out, and_7_out, c_8);
  LED led_14 (.in(and_9_out));
  or or_10 (or_10_out, b_3, c);
  and and_10 (and_10_out, b_7, a_9);
  and and_11 (and_11_out, a_9, c_3);
  or or_11 (or_11_out, a_13, b_13);
  not not_3 (not_3_out, a_15);
  not not_4 (not_4_out, b_15);
  and and_12 (and_12_out, a_19, b_17);
  and and_13 (and_13_out, a_3, or_10_out);
  or or_12 (or_12_out, and_10_out, and_11_out);
  not not_5 (not_5_out, or_11_out);
  and and_14 (and_14_out, not_3_out, not_4_out);
  or or_13 (or_13_out, a_19, and_12_out);
  or or_14 (or_14_out, a_25, a_25);
  LED led_15 (.in(and_13_out));
  LED led_16 (.in(or_12_out));
  LED led_17 (.in(not_5_out));
  LED led_18 (.in(and_14_out));
  LED led_19 (.in(or_13_out));
  LED led_20 (.in(or_14_out));
  and and_15 (and_15_out, b_4, c_2);
  or or_15 (or_15_out, b_8, a_10);
  or or_16 (or_16_out, a_10, c_4);
  and and_16 (and_16_out, a_14, b_14);
  not not_6 (not_6_out, a_16);
  not not_7 (not_7_out, b_16);
  or or_17 (or_17_out, a_20, b_18);
  and and_17 (and_17_out, a_26, a_26);
  LED led_21 (.in(or_18_out));
  or or_18 (or_18_out, a_4, and_15_out);
  and and_18 (and_18_out, or_15_out, or_16_out);
  LED led_22 (.in(not_8_out));
  not not_8 (not_8_out, and_16_out);
  LED led_23 (.in(or_19_out));
  or or_19 (or_19_out, not_6_out, not_7_out);
  LED led_24 (.in(and_19_out));
  and and_19 (and_19_out, a_20, or_17_out);
  LED led_25 (.in(and_17_out));
  LED led_26 (.in(and_18_out));

  // Notes on the sheet:
  //   ~a
  //   a) Conmutatividad
  //   a+b
  //   b+a
  //   b) Asociatividad
  //   c) Identidad
  //   a + 0 = a
  //   d) Anulación
  //   a + 1 = 1
  //   e) Inverso
  //   a + ~a = 1
  //   a + ( b + c)
  //   (a + b) + c
  //   ~a
  //   a*b
  //   b*a
  //   a * 1 = a
  //   a * 0 = 0
  //   a * ~a = 0
  //   a * ( b * c)
  //   (a *  b) *  c
  //   f) Distributividad
  //   a * ( b + c)
  //   a * b + a * c
  //   g) De Morgan
  //   ~(a + b)
  //   ~a * ~b
  //   h) Absorción
  //   a + (a * b) = a
  //   i) Idempotencia
  //   a + a = a
  //   a + ( b * c)
  //   ~(a * b)
  //   ~a + ~b
  //   a * (a + b) = a
  //   a * a = a
  //   (a + b) * (a + c)
endmodule

module Ejercicio_3_1 (
  input  x,
  input  x_2,
  input  y,
  input  x_3,
  input  y_2,
  input  z,
  input  y_3,
  input  z_2,
  input  w,
  input  z_3
);

  wire and_1_out, not_1_out, not_2_out, not_3_out, not_4_out, not_5_out, not_6_out, or_1_out, or_2_out,
       or_3_out;

  not not_1 (not_1_out, y);
  and and_1 (and_1_out, x, not_1_out, z);
  or or_1 (or_1_out, and_1_out, w);
  LED led_1 (.in(or_1_out));
  not not_2 (not_2_out, x_3);
  not not_3 (not_3_out, y_3);
  or or_2 (or_2_out, not_2_out, not_3_out, z_3);
  LED led_2 (.in(or_2_out));
  not not_4 (not_4_out, x_2);
  not not_5 (not_5_out, y_2);
  not not_6 (not_6_out, z_2);
  or or_3 (or_3_out, not_4_out, not_5_out, not_6_out);
  LED led_3 (.in(or_3_out));

  // Notes on the sheet:
  //   a)
  //   Absorcion
  //   (x*~y*z) + w
  //   (x*y*w)+(x*~y*z)+w
  //   Conmutatividad
  //   (x*~y*z)+(x*y*w)+w
  //   (x*~y*z) + w
  //   b)
  //   ~(y*x)+(z*w)+(x*~y)+z
  //   Conmutatividad
  //   ~(y*x)+(x*~y)+(z*w)+z
  //   Absorcion
  //   ~(y*x)+(x*~y)+z
  //   De Morgan
  //   ~y+~x+(x*~y)+z
  //   Conmutatividad
  //   ~x+~y+(x*~y)+z
  //   Absorcion
  //   ~x+~y+z
  //   ~x+~y+z
  //   c)
  //   De Morgan
  //   Absorcion
  //   Absorcion
  //   ~x + ~ y + ~ z 
  //   ~(x*y*z)+(~z*a*b)+(~z*a)
  //   ~x + ~ y + ~ z +(~z*a*b)+(~z*a)
  //   ~x + ~ y + ~ z +(~z*a)
  //   ~x + ~ y + ~ z 
endmodule
